// Logisim project Prática3.circ as structural Verilog: 1 circuit, main circuit main
module main (
  input  A,
  input  B,
  input  C,
  input  D,
  output S
);

  wire nor_1_out, nor_2_out, nor_3_out;

  nor nor_1 (nor_1_out, A, B);
  nor nor_2 (nor_2_out, A, C);
  nor nor_3 (nor_3_out, nor_1_out, nor_2_out);
  nor nor_4 (S, nor_3_out, nor_3_out);
endmodule
