// Logisim project Ex1.circ as structural Verilog: 1 circuit, main circuit main
module main (
  input  A,
  input  B,
  input  C,
  output s
);

  wire and_1_out, and_2_out, and_3_out, not_1_out, not_2_out;

  not not_1 (not_1_out, A);
  and and_1 (and_1_out, A, C, B);
  and and_2 (and_2_out, not_1_out, C);
  not not_2 (not_2_out, B);
  and and_3 (and_3_out, A, not_2_out, C);
  or or_1 (s, and_2_out, and_3_out, and_1_out);
endmodule
