// Logisim project Questão1.circ as structural Verilog: 1 circuit, main circuit main
module main (
  input  [7:0] I,
  input  C1,
  input  C2,
  output [7:0] S1,
  output [7:0] S2,
  output [7:0] S3,
  output [7:0] S4
);

  wire nand_1_out, nand_2_out, nand_3_out, nand_4_out, nand_5_out, nand_6_out, nand_7_out, nand_8_out,
       nand_9_out, nand_10_out, nand_11_out, nand_12_out;

  nand nand_1 (nand_1_out, C2, C2);
  assign S1 = nand_2_out ? I : 8'bz;  // Controlled_Buffer controlled_buffer_1
  nand nand_2 (nand_2_out, nand_4_out, nand_4_out);
  nand nand_3 (nand_3_out, nand_5_out, nand_5_out);
  nand nand_4 (nand_4_out, nand_1_out, nand_6_out);
  nand nand_5 (nand_5_out, C2, nand_10_out);
  nand nand_6 (nand_6_out, C1, C1);
  assign S2 = nand_3_out ? I : 8'bz;  // Controlled_Buffer controlled_buffer_2
  assign S3 = nand_7_out ? I : 8'bz;  // Controlled_Buffer controlled_buffer_3
  nand nand_7 (nand_7_out, nand_8_out, nand_8_out);
  nand nand_8 (nand_8_out, nand_9_out, C1);
  nand nand_9 (nand_9_out, C2, C2);
  nand nand_10 (nand_10_out, C1, C1);
  assign S4 = nand_11_out ? I : 8'bz;  // Controlled_Buffer controlled_buffer_4
  nand nand_11 (nand_11_out, nand_12_out, nand_12_out);
  nand nand_12 (nand_12_out, C2, C1);
endmodule
