// Logisim project Questão2.circ as structural Verilog: 10 circuits, main circuit main
module main (
);

  wire button_1_out, button_2_out, button_3_out, button_4_out, button_5_out, button_6_out, button_7_out,
       button_8_out, button_9_out, button_10_out, button_11_out, button_12_out, button_13_out, button_14_out,
       clock_1_out, contador0_5_1_a, contador0_5_1_b, contador0_5_1_c, contador0_5_1_d, contador0_5_1_next,
       contador0_5_2_a, contador0_5_2_b, contador0_5_2_c, contador0_5_2_d, contador0_5_2_next,
       contador0_9_1_a, contador0_9_1_b, contador0_9_1_c, contador0_9_1_d, contador0_9_1_next,
       contador0_9_2_a, contador0_9_2_b, contador0_9_2_c, contador0_9_2_d, contador0_9_2_next,
       Contador_0_12_a, Contador_0_12_a_2, Contador_0_12_b, Contador_0_12_b_2, Contador_0_12_c,
       Contador_0_12_c_2, Contador_0_12_d, Contador_0_12_d_2, Contador_0_12_next, contador_24_1_a,
       contador_24_1_a_2, contador_24_1_b, contador_24_1_b_2, contador_24_1_c, contador_24_1_c_2,
       contador_24_1_d, contador_24_1_d_2, contador_24_1_next, contador_30_1_a, contador_30_1_a_2,
       contador_30_1_b, contador_30_1_b_2, contador_30_1_c, contador_30_1_c_2, contador_30_1_d,
       contador_30_1_d_2, contador_30_1_next, contador_10000_1_a, contador_10000_1_a_2, contador_10000_1_a_3,
       contador_10000_1_a_4, contador_10000_1_b, contador_10000_1_b_2, contador_10000_1_b_3,
       contador_10000_1_b_4, contador_10000_1_c, contador_10000_1_c_2, contador_10000_1_c_3,
       contador_10000_1_c_4, contador_10000_1_d, contador_10000_1_d_2, contador_10000_1_d_3,
       contador_10000_1_d_4, display7segmentos_1_a_2, display7segmentos_1_b_2, display7segmentos_1_c_2,
       display7segmentos_1_d_2, display7segmentos_1_e, display7segmentos_1_f, display7segmentos_1_g,
       display7segmentos_2_a_2, display7segmentos_2_b_2, display7segmentos_2_c_2, display7segmentos_2_d_2,
       display7segmentos_2_e, display7segmentos_2_f, display7segmentos_2_g, display7segmentos_3_a_2,
       display7segmentos_3_b_2, display7segmentos_3_c_2, display7segmentos_3_d_2, display7segmentos_3_e,
       display7segmentos_3_f, display7segmentos_3_g, display7segmentos_4_a_2, display7segmentos_4_b_2,
       display7segmentos_4_c_2, display7segmentos_4_d_2, display7segmentos_4_e, display7segmentos_4_f,
       display7segmentos_4_g, display7segmentos_5_a_2, display7segmentos_5_b_2, display7segmentos_5_c_2,
       display7segmentos_5_d_2, display7segmentos_5_e, display7segmentos_5_f, display7segmentos_5_g,
       display7segmentos_6_a_2, display7segmentos_6_b_2, display7segmentos_6_c_2, display7segmentos_6_d_2,
       display7segmentos_6_e, display7segmentos_6_f, display7segmentos_6_g, display7segmentos_7_a_2,
       display7segmentos_7_b_2, display7segmentos_7_c_2, display7segmentos_7_d_2, display7segmentos_7_e,
       display7segmentos_7_f, display7segmentos_7_g, display7segmentos_8_a_2, display7segmentos_8_b_2,
       display7segmentos_8_c_2, display7segmentos_8_d_2, display7segmentos_8_e, display7segmentos_8_f,
       display7segmentos_8_g, display7segmentos_9_a_2, display7segmentos_9_b_2, display7segmentos_9_c_2,
       display7segmentos_9_d_2, display7segmentos_9_e, display7segmentos_9_f, display7segmentos_9_g,
       display7segmentos_10_a_2, display7segmentos_10_b_2, display7segmentos_10_c_2,
       display7segmentos_10_d_2, display7segmentos_10_e, display7segmentos_10_f, display7segmentos_10_g,
       display7segmentos_11_a_2, display7segmentos_11_b_2, display7segmentos_11_c_2,
       display7segmentos_11_d_2, display7segmentos_11_e, display7segmentos_11_f, display7segmentos_11_g,
       display7segmentos_12_a_2, display7segmentos_12_b_2, display7segmentos_12_c_2,
       display7segmentos_12_d_2, display7segmentos_12_e, display7segmentos_12_f, display7segmentos_12_g,
       display7segmentos_13_a_2, display7segmentos_13_b_2, display7segmentos_13_c_2,
       display7segmentos_13_d_2, display7segmentos_13_e, display7segmentos_13_f, display7segmentos_13_g,
       display7segmentos_14_a_2, display7segmentos_14_b_2, display7segmentos_14_c_2,
       display7segmentos_14_d_2, display7segmentos_14_e, display7segmentos_14_f, display7segmentos_14_g,
       mudames_1_out_13, or_1_out, or_2_out, or_3_out;

  Button button_1 (.out(button_1_out));
  Button button_2 (.out(button_2_out));
  display7segmentos display7segmentos_1 (
    .A(contador_30_1_a), .B(contador_30_1_b), .C(contador_30_1_c), .D(contador_30_1_d),
    .a_2(display7segmentos_1_a_2), .b_2(display7segmentos_1_b_2), .c_2(display7segmentos_1_c_2),
    .d_2(display7segmentos_1_d_2), .e(display7segmentos_1_e), .f(display7segmentos_1_f),
    .g(display7segmentos_1_g));
  or or_1 (or_1_out, button_1_out, mudames_1_out_13);
  or or_2 (or_2_out, button_2_out, mudames_1_out_13);
  _7_Segment_Display u_7_segment_display_1 (
    .g(display7segmentos_2_g), .f(display7segmentos_2_f), .a(display7segmentos_2_a_2),
    .b(display7segmentos_2_b_2), .e(display7segmentos_2_e), .d(display7segmentos_2_d_2),
    .c(display7segmentos_2_c_2));  // open: dp
  _7_Segment_Display u_7_segment_display_2 (
    .g(display7segmentos_1_g), .f(display7segmentos_1_f), .a(display7segmentos_1_a_2),
    .b(display7segmentos_1_b_2), .e(display7segmentos_1_e), .d(display7segmentos_1_d_2),
    .c(display7segmentos_1_c_2));  // open: dp
  Contador_30 contador_30_1 (
    .Fin(contador_24_1_next), .Clear(or_1_out), .Clear_2(or_2_out), .D(contador_30_1_d), .C(contador_30_1_c),
    .B(contador_30_1_b), .A(contador_30_1_a), .D_2(contador_30_1_d_2), .C_2(contador_30_1_c_2),
    .B_2(contador_30_1_b_2), .A_2(contador_30_1_a_2), .NEXT(contador_30_1_next));
  display7segmentos display7segmentos_2 (
    .A(contador_30_1_a_2), .B(contador_30_1_b_2), .C(contador_30_1_c_2), .D(contador_30_1_d_2),
    .a_2(display7segmentos_2_a_2), .b_2(display7segmentos_2_b_2), .c_2(display7segmentos_2_c_2),
    .d_2(display7segmentos_2_d_2), .e(display7segmentos_2_e), .f(display7segmentos_2_f),
    .g(display7segmentos_2_g));
  display7segmentos display7segmentos_3 (
    .A(Contador_0_12_a), .B(Contador_0_12_b), .C(Contador_0_12_c), .D(Contador_0_12_d),
    .a_2(display7segmentos_3_a_2), .b_2(display7segmentos_3_b_2), .c_2(display7segmentos_3_c_2),
    .d_2(display7segmentos_3_d_2), .e(display7segmentos_3_e), .f(display7segmentos_3_f),
    .g(display7segmentos_3_g));
  or or_3 (or_3_out, contador_30_1_next, mudames_1_out_13);
  mudaMes mudames_1 (
    .in_1(contador_30_1_c), .in_2(contador_30_1_d), .in_3(contador_30_1_a_2), .in_4(contador_30_1_b_2),
    .in_5(contador_30_1_c_2), .in_6(contador_30_1_d_2), .in_7(Contador_0_12_c), .in_8(Contador_0_12_d),
    .in_9(Contador_0_12_a_2), .in_10(Contador_0_12_b_2), .in_11(Contador_0_12_c_2),
    .in_12(Contador_0_12_d_2), .out_13(mudames_1_out_13));
  _7_Segment_Display u_7_segment_display_3 (
    .g(display7segmentos_4_g), .f(display7segmentos_4_f), .a(display7segmentos_4_a_2),
    .b(display7segmentos_4_b_2), .e(display7segmentos_4_e), .d(display7segmentos_4_d_2),
    .c(display7segmentos_4_c_2));  // open: dp
  _7_Segment_Display u_7_segment_display_4 (
    .g(display7segmentos_3_g), .f(display7segmentos_3_f), .a(display7segmentos_3_a_2),
    .b(display7segmentos_3_b_2), .e(display7segmentos_3_e), .d(display7segmentos_3_d_2),
    .c(display7segmentos_3_c_2));  // open: dp
  Button button_3 (.out(button_3_out));
  Button button_4 (.out(button_4_out));
  Contador_12 Contador_0_12 (
    .Fin(or_3_out), .Clear(button_4_out), .Clear_2(button_3_out), .D(Contador_0_12_d), .C(Contador_0_12_c),
    .B(Contador_0_12_b), .A(Contador_0_12_a), .D_2(Contador_0_12_d_2), .C_2(Contador_0_12_c_2),
    .B_2(Contador_0_12_b_2), .A_2(Contador_0_12_a_2), .NEXT(Contador_0_12_next));
  display7segmentos display7segmentos_4 (
    .A(Contador_0_12_a_2), .B(Contador_0_12_b_2), .C(Contador_0_12_c_2), .D(Contador_0_12_d_2),
    .a_2(display7segmentos_4_a_2), .b_2(display7segmentos_4_b_2), .c_2(display7segmentos_4_c_2),
    .d_2(display7segmentos_4_d_2), .e(display7segmentos_4_e), .f(display7segmentos_4_f),
    .g(display7segmentos_4_g));
  display7segmentos display7segmentos_5 (
    .A(contador_10000_1_a_2), .B(contador_10000_1_b_2), .C(contador_10000_1_c_2), .D(contador_10000_1_d_2),
    .a_2(display7segmentos_5_a_2), .b_2(display7segmentos_5_b_2), .c_2(display7segmentos_5_c_2),
    .d_2(display7segmentos_5_d_2), .e(display7segmentos_5_e), .f(display7segmentos_5_f),
    .g(display7segmentos_5_g));
  _7_Segment_Display u_7_segment_display_5 (
    .g(display7segmentos_5_g), .f(display7segmentos_5_f), .a(display7segmentos_5_a_2),
    .b(display7segmentos_5_b_2), .e(display7segmentos_5_e), .d(display7segmentos_5_d_2),
    .c(display7segmentos_5_c_2));  // open: dp
  _7_Segment_Display u_7_segment_display_6 (
    .g(display7segmentos_6_g), .f(display7segmentos_6_f), .a(display7segmentos_6_a_2),
    .b(display7segmentos_6_b_2), .e(display7segmentos_6_e), .d(display7segmentos_6_d_2),
    .c(display7segmentos_6_c_2));  // open: dp
  _7_Segment_Display u_7_segment_display_7 (
    .g(display7segmentos_8_g), .f(display7segmentos_8_f), .a(display7segmentos_8_a_2),
    .b(display7segmentos_8_b_2), .e(display7segmentos_8_e), .d(display7segmentos_8_d_2),
    .c(display7segmentos_8_c_2));  // open: dp
  _7_Segment_Display u_7_segment_display_8 (
    .g(display7segmentos_7_g), .f(display7segmentos_7_f), .a(display7segmentos_7_a_2),
    .b(display7segmentos_7_b_2), .e(display7segmentos_7_e), .d(display7segmentos_7_d_2),
    .c(display7segmentos_7_c_2));  // open: dp
  Button button_5 (.out(button_5_out));
  Button button_6 (.out(button_6_out));
  Button button_7 (.out(button_7_out));
  Button button_8 (.out(button_8_out));
  display7segmentos display7segmentos_6 (
    .A(contador_10000_1_a_4), .B(contador_10000_1_b_4), .C(contador_10000_1_c_4), .D(contador_10000_1_d_4),
    .a_2(display7segmentos_6_a_2), .b_2(display7segmentos_6_b_2), .c_2(display7segmentos_6_c_2),
    .d_2(display7segmentos_6_d_2), .e(display7segmentos_6_e), .f(display7segmentos_6_f),
    .g(display7segmentos_6_g));
  display7segmentos display7segmentos_7 (
    .A(contador_10000_1_a), .B(contador_10000_1_b), .C(contador_10000_1_c), .D(contador_10000_1_d),
    .a_2(display7segmentos_7_a_2), .b_2(display7segmentos_7_b_2), .c_2(display7segmentos_7_c_2),
    .d_2(display7segmentos_7_d_2), .e(display7segmentos_7_e), .f(display7segmentos_7_f),
    .g(display7segmentos_7_g));
  Contador_10000 contador_10000_1 (
    .Fin(Contador_0_12_next), .Clear(button_5_out), .Clear_2(button_6_out), .Clear_3(button_7_out),
    .Clear_4(button_8_out), .D_2(contador_10000_1_d_2), .C_2(contador_10000_1_c_2),
    .B_2(contador_10000_1_b_2), .A_2(contador_10000_1_a_2), .D_4(contador_10000_1_d_4),
    .C_4(contador_10000_1_c_4), .B_4(contador_10000_1_b_4), .A_4(contador_10000_1_a_4),
    .D(contador_10000_1_d), .C(contador_10000_1_c), .B(contador_10000_1_b), .A(contador_10000_1_a),
    .D_3(contador_10000_1_d_3), .C_3(contador_10000_1_c_3), .B_3(contador_10000_1_b_3),
    .A_3(contador_10000_1_a_3));  // open: NEXT
  display7segmentos display7segmentos_8 (
    .A(contador_10000_1_a_3), .B(contador_10000_1_b_3), .C(contador_10000_1_c_3), .D(contador_10000_1_d_3),
    .a_2(display7segmentos_8_a_2), .b_2(display7segmentos_8_b_2), .c_2(display7segmentos_8_c_2),
    .d_2(display7segmentos_8_d_2), .e(display7segmentos_8_e), .f(display7segmentos_8_f),
    .g(display7segmentos_8_g));
  Button button_9 (.out(button_9_out));
  Button button_10 (.out(button_10_out));
  Contador_24 contador_24_1 (
    .Fin(contador0_5_1_next), .Clear(button_9_out), .Clear_2(button_10_out), .D(contador_24_1_d),
    .C(contador_24_1_c), .B(contador_24_1_b), .A(contador_24_1_a), .D_2(contador_24_1_d_2),
    .C_2(contador_24_1_c_2), .B_2(contador_24_1_b_2), .A_2(contador_24_1_a_2), .NEXT(contador_24_1_next));
  display7segmentos display7segmentos_9 (
    .A(contador_24_1_a), .B(contador_24_1_b), .C(contador_24_1_c), .D(contador_24_1_d),
    .a_2(display7segmentos_9_a_2), .b_2(display7segmentos_9_b_2), .c_2(display7segmentos_9_c_2),
    .d_2(display7segmentos_9_d_2), .e(display7segmentos_9_e), .f(display7segmentos_9_f),
    .g(display7segmentos_9_g));
  display7segmentos display7segmentos_10 (
    .A(contador_24_1_a_2), .B(contador_24_1_b_2), .C(contador_24_1_c_2), .D(contador_24_1_d_2),
    .a_2(display7segmentos_10_a_2), .b_2(display7segmentos_10_b_2), .c_2(display7segmentos_10_c_2),
    .d_2(display7segmentos_10_d_2), .e(display7segmentos_10_e), .f(display7segmentos_10_f),
    .g(display7segmentos_10_g));
  _7_Segment_Display u_7_segment_display_9 (
    .g(display7segmentos_9_g), .f(display7segmentos_9_f), .a(display7segmentos_9_a_2),
    .b(display7segmentos_9_b_2), .e(display7segmentos_9_e), .d(display7segmentos_9_d_2),
    .c(display7segmentos_9_c_2));  // open: dp
  Button button_11 (.out(button_11_out));
  _7_Segment_Display u_7_segment_display_10 (
    .g(display7segmentos_10_g), .f(display7segmentos_10_f), .a(display7segmentos_10_a_2),
    .b(display7segmentos_10_b_2), .e(display7segmentos_10_e), .d(display7segmentos_10_d_2),
    .c(display7segmentos_10_c_2));  // open: dp
  display7segmentos display7segmentos_11 (
    .A(contador0_5_1_a), .B(contador0_5_1_b), .C(contador0_5_1_c), .D(contador0_5_1_d),
    .a_2(display7segmentos_11_a_2), .b_2(display7segmentos_11_b_2), .c_2(display7segmentos_11_c_2),
    .d_2(display7segmentos_11_d_2), .e(display7segmentos_11_e), .f(display7segmentos_11_f),
    .g(display7segmentos_11_g));
  Contador0_5 contador0_5_1 (
    .Fin(contador0_9_1_next), .Clear(button_11_out), .D(contador0_5_1_d), .C(contador0_5_1_c),
    .B(contador0_5_1_b), .A(contador0_5_1_a), .NEXT(contador0_5_1_next));
  Button button_12 (.out(button_12_out));
  Contador0_9 contador0_9_1 (
    .Fin(contador0_5_2_next), .Clear(button_12_out), .D(contador0_9_1_d), .C(contador0_9_1_c),
    .B(contador0_9_1_b), .A(contador0_9_1_a), .NEXT(contador0_9_1_next));
  _7_Segment_Display u_7_segment_display_11 (
    .g(display7segmentos_12_g), .f(display7segmentos_12_f), .a(display7segmentos_12_a_2),
    .b(display7segmentos_12_b_2), .e(display7segmentos_12_e), .d(display7segmentos_12_d_2),
    .c(display7segmentos_12_c_2));  // open: dp
  _7_Segment_Display u_7_segment_display_12 (
    .g(display7segmentos_11_g), .f(display7segmentos_11_f), .a(display7segmentos_11_a_2),
    .b(display7segmentos_11_b_2), .e(display7segmentos_11_e), .d(display7segmentos_11_d_2),
    .c(display7segmentos_11_c_2));  // open: dp
  display7segmentos display7segmentos_12 (
    .A(contador0_9_1_a), .B(contador0_9_1_b), .C(contador0_9_1_c), .D(contador0_9_1_d),
    .a_2(display7segmentos_12_a_2), .b_2(display7segmentos_12_b_2), .c_2(display7segmentos_12_c_2),
    .d_2(display7segmentos_12_d_2), .e(display7segmentos_12_e), .f(display7segmentos_12_f),
    .g(display7segmentos_12_g));
  Button button_13 (.out(button_13_out));
  _7_Segment_Display u_7_segment_display_13 (
    .g(display7segmentos_13_g), .f(display7segmentos_13_f), .a(display7segmentos_13_a_2),
    .b(display7segmentos_13_b_2), .e(display7segmentos_13_e), .d(display7segmentos_13_d_2),
    .c(display7segmentos_13_c_2));  // open: dp
  display7segmentos display7segmentos_13 (
    .A(contador0_5_2_a), .B(contador0_5_2_b), .C(contador0_5_2_c), .D(contador0_5_2_d),
    .a_2(display7segmentos_13_a_2), .b_2(display7segmentos_13_b_2), .c_2(display7segmentos_13_c_2),
    .d_2(display7segmentos_13_d_2), .e(display7segmentos_13_e), .f(display7segmentos_13_f),
    .g(display7segmentos_13_g));
  Contador0_5 contador0_5_2 (
    .Fin(contador0_9_2_next), .Clear(button_13_out), .D(contador0_5_2_d), .C(contador0_5_2_c),
    .B(contador0_5_2_b), .A(contador0_5_2_a), .NEXT(contador0_5_2_next));
  _7_Segment_Display u_7_segment_display_14 (
    .g(display7segmentos_14_g), .f(display7segmentos_14_f), .a(display7segmentos_14_a_2),
    .b(display7segmentos_14_b_2), .e(display7segmentos_14_e), .d(display7segmentos_14_d_2),
    .c(display7segmentos_14_c_2));  // open: dp
  Clock clock_1 (.out(clock_1_out));
  Button button_14 (.out(button_14_out));
  Contador0_9 contador0_9_2 (
    .Fin(clock_1_out), .Clear(button_14_out), .D(contador0_9_2_d), .C(contador0_9_2_c), .B(contador0_9_2_b),
    .A(contador0_9_2_a), .NEXT(contador0_9_2_next));
  display7segmentos display7segmentos_14 (
    .A(contador0_9_2_a), .B(contador0_9_2_b), .C(contador0_9_2_c), .D(contador0_9_2_d),
    .a_2(display7segmentos_14_a_2), .b_2(display7segmentos_14_b_2), .c_2(display7segmentos_14_c_2),
    .d_2(display7segmentos_14_d_2), .e(display7segmentos_14_e), .f(display7segmentos_14_f),
    .g(display7segmentos_14_g));

  // Notes on the sheet:
  //   Modulador de 7 segmentos
  //   Contador 0-30
  //   Circuito que calcula mudança de mes
  //   Modulador de 7 segmentos
  //   Modulador de 7 segmentos
  //   Modulador de 7 segmentos
  //   Modulador de 7 segmentos
  //   Modulador de 7 segmentos
  //   Contadore de anos
  //   Modulador de 7 segmentos
  //   Modulador de 7 segmentos
  //   Contador e horas
  //   Modulador de 7 segmentos
  //   Modulador de 7 segmentos
  //   contador de 0-5
  //   Modulador de 7 segmentos
  //   contador de 0-9
  //   Modulador de 7 segmentos
  //   contador de 0-5
  //   Modulador de 7 segmentos
  //   aos minutos que muda as horas
  //   contador de 0-9
  //   a cada ciclo de clock (1 to 0) muda um segundo
  //   quando os segundos atingirem 60 ativa um gatilho
  //   que muda os minutos e a mesma logica se aplica
  //   quando as horas atingem 24 ativa-se o circuito que muda o dia
  //   quando o dia atinge a 28 ou 30 ou 31 dias dependendo do mes
  //   aciona o circuito que muda o mes e este ao atingir o fim de 12 meses aciona a troca de ano
  //   Modulador de 7 segmentos
endmodule

module display7segmentos (
  input  A,
  input  B,
  input  C,
  input  D,
  output a_2,
  output b_2,
  output c_2,
  output d_2,
  output e,
  output f,
  output g
);

  wire and_1_out, and_2_out, and_3_out, and_4_out, and_5_out, and_6_out, and_7_out, and_8_out, and_9_out,
       and_10_out, and_11_out, and_12_out, and_13_out, not_1_out, not_2_out, not_3_out, not_4_out, not_5_out,
       not_6_out, not_7_out, not_8_out, not_9_out, not_10_out, not_11_out, not_12_out, not_13_out,
       not_14_out, not_15_out, not_16_out, not_17_out, or_1_out, or_3_out, or_6_out, or_8_out, xnor_1_out,
       xor_1_out;

  or or_1 (or_1_out, A, C);
  or or_2 (a_2, or_1_out, xnor_1_out);
  xnor xnor_1 (xnor_1_out, B, D);
  not not_1 (not_1_out, D);
  not not_2 (not_2_out, B);
  or or_3 (or_3_out, not_2_out, and_2_out);
  not not_3 (not_3_out, C);
  and and_1 (and_1_out, D, C);
  and and_2 (and_2_out, not_1_out, not_3_out);
  or or_4 (b_2, or_3_out, and_1_out);
  not not_4 (not_4_out, C);
  or or_5 (c_2, not_4_out, B, D);
  not not_5 (not_5_out, B);
  not not_6 (not_6_out, D);
  not not_7 (not_7_out, B);
  and and_3 (and_3_out, not_7_out, not_6_out);
  or or_6 (or_6_out, A, and_3_out);
  or or_7 (d_2, or_6_out, and_4_out, or_8_out);
  not not_8 (not_8_out, D);
  and and_4 (and_4_out, not_5_out, C);
  and and_5 (and_5_out, C, not_8_out);
  or or_8 (or_8_out, and_5_out, and_6_out);
  not not_9 (not_9_out, C);
  and and_6 (and_6_out, B, not_9_out, D);
  not not_10 (not_10_out, D);
  not not_11 (not_11_out, B);
  and and_7 (and_7_out, not_11_out, not_10_out);
  not not_12 (not_12_out, D);
  and and_8 (and_8_out, B, A);
  and and_9 (and_9_out, C, not_12_out);
  or or_9 (e, and_7_out, and_9_out, and_8_out);
  not not_13 (not_13_out, C);
  not not_14 (not_14_out, D);
  and and_10 (and_10_out, not_13_out, not_14_out);
  not not_15 (not_15_out, C);
  and and_11 (and_11_out, not_15_out, B);
  or or_10 (f, A, and_10_out, and_11_out, and_12_out);
  not not_16 (not_16_out, D);
  not not_17 (not_17_out, D);
  and and_12 (and_12_out, B, not_16_out);
  and and_13 (and_13_out, not_17_out, C);
  or or_11 (g, A, and_13_out, xor_1_out);
  xor xor_1 (xor_1_out, C, B);

  // Notes on the sheet:
  //   Modulador de BCD8421 para  7segmentos
endmodule

module Contador0_5 (
  input  Fin,
  input  Clear,
  output D,
  output C,
  output B,
  output A,
  output NEXT
);

  wire not_1_out, or_1_out;

  or or_1 (or_1_out, Clear, NEXT);
  T_Flip_Flop #(.trigger("falling")) t_ff_1 (.clk(Fin), .T(1'b1), .Q(D), .reset(or_1_out));  // open: Qn, preset, en
  T_Flip_Flop #(.trigger("falling")) t_ff_2 (.clk(D), .T(1'b1), .Q(C), .reset(or_1_out));  // open: Qn, preset, en
  not not_1 (not_1_out, D);
  and and_1 (NEXT, not_1_out, C, B);
  T_Flip_Flop #(.trigger("falling")) t_ff_3 (.clk(C), .T(1'b1), .Q(B), .reset(or_1_out));  // open: Qn, preset, en
  T_Flip_Flop #(.trigger("falling")) t_ff_4 (.clk(B), .T(1'b1), .Q(A), .reset(or_1_out));  // open: Qn, preset, en

  // Notes on the sheet:
  //   Contador de 0-5
  //   verificador de valor se ==6 reseta
  //   Flip flop T para alternar a contagem
  //   ativam quando sai do 1 e vai para o 0
endmodule

module Contador0_9 (
  input  Fin,
  input  Clear,
  output D,
  output C,
  output B,
  output A,
  output NEXT
);

  wire not_1_out, not_2_out, or_1_out;

  or or_1 (or_1_out, Clear, NEXT);
  T_Flip_Flop #(.trigger("falling")) t_ff_1 (.clk(Fin), .T(1'b1), .Q(D), .reset(or_1_out));  // open: Qn, preset, en
  T_Flip_Flop #(.trigger("falling")) t_ff_2 (.clk(D), .T(1'b1), .Q(C), .reset(or_1_out));  // open: Qn, preset, en
  not not_1 (not_1_out, D);
  and and_1 (NEXT, not_1_out, C, not_2_out, A);
  T_Flip_Flop #(.trigger("falling")) t_ff_3 (.clk(C), .T(1'b1), .Q(B), .reset(or_1_out));  // open: Qn, preset, en
  not not_2 (not_2_out, B);
  T_Flip_Flop #(.trigger("falling")) t_ff_4 (.clk(B), .T(1'b1), .Q(A), .reset(or_1_out));  // open: Qn, preset, en

  // Notes on the sheet:
  //   verificador de valor se ==10 reseta
  //   Flip flop T para alternar a contagem
  //   ativam quando sai do 1 e vai para o 0
endmodule

module Contador0_2 (
  input  Fin,
  input  Clear,
  output D,
  output C,
  output B,
  output A,
  output NEXT
);

  wire not_1_out, or_1_out;

  or or_1 (or_1_out, Clear, NEXT);
  T_Flip_Flop #(.trigger("falling")) t_ff_1 (.clk(Fin), .T(1'b1), .Q(D), .reset(or_1_out));  // open: Qn, preset, en
  T_Flip_Flop #(.trigger("falling")) t_ff_2 (.clk(D), .T(1'b1), .Q(C), .reset(or_1_out));  // open: Qn, preset, en
  and and_1 (NEXT, D, C, not_1_out);
  T_Flip_Flop #(.trigger("falling")) t_ff_3 (.clk(C), .T(1'b1), .Q(B), .reset(or_1_out));  // open: Qn, preset, en
  not not_1 (not_1_out, B);
  T_Flip_Flop #(.trigger("falling")) t_ff_4 (.clk(B), .T(1'b1), .Q(A), .reset(or_1_out));  // open: Qn, preset, en

  // Notes on the sheet:
  //   verificador de valor se ==3 reseta
  //   Flip flop T para alternar a contagem
  //   ativam quando sai do 1 e vai para o 0
endmodule

module Contador_24 (
  input  Fin,
  input  Clear,
  input  Clear_2,
  output D,
  output C,
  output B,
  output A,
  output D_2,
  output C_2,
  output B_2,
  output A_2,
  output NEXT
);

  wire and_1_out, and_3_out, and_4_out, not_1_out, not_2_out, not_3_out, not_4_out, not_5_out, or_1_out,
       or_2_out;

  or or_1 (or_1_out, Clear_2, NEXT);
  T_Flip_Flop #(.trigger("falling")) t_ff_1 (
    .clk(and_4_out), .T(1'b1), .Q(D), .reset(or_1_out));  // open: Qn, preset, en
  T_Flip_Flop #(.trigger("falling")) t_ff_2 (.clk(D), .T(1'b1), .Q(C), .reset(or_1_out));  // open: Qn, preset, en
  not not_1 (not_1_out, D);
  and and_1 (and_1_out, not_1_out, C);
  T_Flip_Flop #(.trigger("falling")) t_ff_3 (.clk(C), .T(1'b1), .Q(B), .reset(or_1_out));  // open: Qn, preset, en
  T_Flip_Flop #(.trigger("falling")) t_ff_4 (.clk(B), .T(1'b1), .Q(A), .reset(or_1_out));  // open: Qn, preset, en
  and and_2 (NEXT, and_1_out, and_3_out);
  not not_2 (not_2_out, D_2);
  not not_3 (not_3_out, C_2);
  and and_3 (and_3_out, not_2_out, not_3_out, B_2);
  or or_2 (or_2_out, Clear, NEXT, and_4_out);
  T_Flip_Flop #(.trigger("falling")) t_ff_5 (.clk(Fin), .T(1'b1), .Q(D_2), .reset(or_2_out));  // open: Qn, preset, en
  T_Flip_Flop #(.trigger("falling")) t_ff_6 (.clk(D_2), .T(1'b1), .Q(C_2), .reset(or_2_out));  // open: Qn, preset, en
  not not_4 (not_4_out, D_2);
  and and_4 (and_4_out, not_4_out, C_2, not_5_out, A_2);
  T_Flip_Flop #(.trigger("falling")) t_ff_7 (.clk(C_2), .T(1'b1), .Q(B_2), .reset(or_2_out));  // open: Qn, preset, en
  not not_5 (not_5_out, B_2);
  T_Flip_Flop #(.trigger("falling")) t_ff_8 (.clk(B_2), .T(1'b1), .Q(A_2), .reset(or_2_out));  // open: Qn, preset, en

  // Notes on the sheet:
  //   Sub contador das dezenas 0-2 
  //   verifica se ==2 
  //   verificador se dezena== 2 e  unidade == 4 reseta dezenas e unidades
  //   sub contador das unidades 0-9
  //   verifica se ==4 
  //   verificador se ==10 similar ao 0-9
endmodule

module Contador_30 (
  input  Fin,
  input  Clear,
  input  Clear_2,
  output D,
  output C,
  output B,
  output A,
  output D_2,
  output C_2,
  output B_2,
  output A_2,
  output NEXT
);

  wire and_1_out, and_3_out, and_4_out, not_1_out, not_2_out, not_3_out, not_4_out, not_5_out, not_6_out,
       or_1_out, or_2_out, or_3_out;

  or or_1 (or_1_out, Clear, NEXT);
  T_Flip_Flop #(.trigger("falling")) t_ff_1 (
    .clk(and_4_out), .T(1'b1), .Q(D), .reset(or_1_out));  // open: Qn, preset, en
  T_Flip_Flop #(.trigger("falling")) t_ff_2 (.clk(D), .T(1'b1), .Q(C), .reset(or_1_out));  // open: Qn, preset, en
  and and_1 (and_1_out, D, C, not_1_out);
  T_Flip_Flop #(.trigger("falling")) t_ff_3 (.clk(C), .T(1'b1), .Q(B), .reset(or_1_out));  // open: Qn, preset, en
  not not_1 (not_1_out, B);
  T_Flip_Flop #(.trigger("falling")) t_ff_4 (.clk(B), .T(1'b1), .Q(A), .reset(or_1_out));  // open: Qn, preset, en
  and and_2 (NEXT, and_1_out, and_3_out);
  or or_2 (or_2_out, Fin, or_1_out);
  or or_3 (or_3_out, Clear_2, NEXT, and_4_out);
  T_Flip_Flop #(.trigger("falling")) t_ff_5 (
    .clk(or_2_out), .T(1'b1), .Q(D_2), .reset(or_3_out));  // open: Qn, preset, en
  not not_2 (not_2_out, C_2);
  and and_3 (and_3_out, D_2, not_2_out, not_4_out, not_3_out);
  not not_3 (not_3_out, A_2);
  not not_4 (not_4_out, B_2);
  T_Flip_Flop #(.trigger("falling")) t_ff_6 (.clk(D_2), .T(1'b1), .Q(C_2), .reset(or_3_out));  // open: Qn, preset, en
  not not_5 (not_5_out, D_2);
  not not_6 (not_6_out, B_2);
  and and_4 (and_4_out, not_5_out, C_2, not_6_out, A_2);
  T_Flip_Flop #(.trigger("falling")) t_ff_7 (.clk(C_2), .T(1'b1), .Q(B_2), .reset(or_3_out));  // open: Qn, preset, en
  T_Flip_Flop #(.trigger("falling")) t_ff_8 (.clk(B_2), .T(1'b1), .Q(A_2), .reset(or_3_out));  // open: Qn, preset, en

  // Notes on the sheet:
  //   sub contador dezenas 0-3
  //   verifica se a dezena == 3
  //   se dezena ==3 e unidade == 1 reseta dezena e unidade
  //   flip flop T
  //   Como demais contadores
  //   sub contador unidades 0-9
  //   verifica se a unidade ==1
  //   verificador se ==10 similar ao contadpr 0-9
endmodule

module Contador_12 (
  input  Fin,
  input  Clear,
  input  Clear_2,
  output D,
  output C,
  output B,
  output A,
  output D_2,
  output C_2,
  output B_2,
  output A_2,
  output NEXT
);

  wire and_1_out, and_3_out, and_4_out, not_1_out, not_2_out, not_3_out, or_1_out, or_2_out;

  or or_1 (or_1_out, Clear, NEXT);
  T_Flip_Flop #(.trigger("falling")) t_ff_1 (
    .clk(and_4_out), .T(1'b1), .Q(D), .reset(or_1_out));  // open: Qn, preset, en
  T_Flip_Flop #(.trigger("falling")) t_ff_2 (.clk(D), .T(1'b1), .Q(C), .reset(or_1_out));  // open: Qn, preset, en
  not not_1 (not_1_out, C);
  and and_1 (and_1_out, D, not_1_out);
  T_Flip_Flop #(.trigger("falling")) t_ff_3 (.clk(C), .T(1'b1), .Q(B), .reset(or_1_out));  // open: Qn, preset, en
  T_Flip_Flop #(.trigger("falling")) t_ff_4 (.clk(B), .T(1'b1), .Q(A), .reset(or_1_out));  // open: Qn, preset, en
  and and_2 (NEXT, and_1_out, and_3_out);
  or or_2 (or_2_out, Clear_2, NEXT, and_4_out);
  T_Flip_Flop #(.trigger("falling")) t_ff_5 (.clk(Fin), .T(1'b1), .Q(D_2), .reset(or_2_out));  // open: Qn, preset, en
  and and_3 (and_3_out, D_2, C_2);
  T_Flip_Flop #(.trigger("falling")) t_ff_6 (.clk(D_2), .T(1'b1), .Q(C_2), .reset(or_2_out));  // open: Qn, preset, en
  not not_2 (not_2_out, D_2);
  not not_3 (not_3_out, B_2);
  and and_4 (and_4_out, not_2_out, C_2, not_3_out, A_2);
  T_Flip_Flop #(.trigger("falling")) t_ff_7 (.clk(C_2), .T(1'b1), .Q(B_2), .reset(or_2_out));  // open: Qn, preset, en
  T_Flip_Flop #(.trigger("falling")) t_ff_8 (.clk(B_2), .T(1'b1), .Q(A_2), .reset(or_2_out));  // open: Qn, preset, en

  // Notes on the sheet:
  //   sub contador das dezenas
  //   verifica se dezena ==1
  //   se dezena ==1 e unidade ==2 reseta unidades de dezenas
  //   flip flop T
  //   Como demais contadores
  //   sub contador das unidades
  //   verifica se unidade ==2
  //   verifica se unidade ==10 como no contador 0-9
endmodule

module Contador_10000 (
  input  Fin,
  input  Clear,
  input  Clear_2,
  input  Clear_3,
  input  Clear_4,
  output D,
  output C,
  output B,
  output A,
  output D_2,
  output C_2,
  output B_2,
  output A_2,
  output D_3,
  output C_3,
  output B_3,
  output A_3,
  output D_4,
  output C_4,
  output B_4,
  output A_4,
  output NEXT
);

  wire and_2_out, and_3_out, and_4_out, not_1_out, not_2_out, not_3_out, not_4_out, not_5_out, not_6_out,
       not_7_out, not_8_out, or_1_out, or_2_out, or_3_out, or_4_out;

  or or_1 (or_1_out, Clear_2, NEXT);
  T_Flip_Flop #(.trigger("falling")) t_ff_1 (
    .clk(and_2_out), .T(1'b1), .Q(D_2), .reset(or_1_out));  // open: Qn, preset, en
  T_Flip_Flop #(.trigger("falling")) t_ff_2 (.clk(D_2), .T(1'b1), .Q(C_2), .reset(or_1_out));  // open: Qn, preset, en
  not not_1 (not_1_out, D_2);
  and and_1 (NEXT, not_1_out, C_2, not_2_out, A_2);
  T_Flip_Flop #(.trigger("falling")) t_ff_3 (.clk(C_2), .T(1'b1), .Q(B_2), .reset(or_1_out));  // open: Qn, preset, en
  not not_2 (not_2_out, B_2);
  T_Flip_Flop #(.trigger("falling")) t_ff_4 (.clk(B_2), .T(1'b1), .Q(A_2), .reset(or_1_out));  // open: Qn, preset, en
  or or_2 (or_2_out, Clear_4, and_2_out);
  T_Flip_Flop #(.trigger("falling")) t_ff_5 (
    .clk(and_3_out), .T(1'b1), .Q(D_4), .reset(or_2_out));  // open: Qn, preset, en
  T_Flip_Flop #(.trigger("falling")) t_ff_6 (.clk(D_4), .T(1'b1), .Q(C_4), .reset(or_2_out));  // open: Qn, preset, en
  not not_3 (not_3_out, B_4);
  not not_4 (not_4_out, D_4);
  and and_2 (and_2_out, not_4_out, C_4, not_3_out, A_4);
  T_Flip_Flop #(.trigger("falling")) t_ff_7 (.clk(C_4), .T(1'b1), .Q(B_4), .reset(or_2_out));  // open: Qn, preset, en
  T_Flip_Flop #(.trigger("falling")) t_ff_8 (.clk(B_4), .T(1'b1), .Q(A_4), .reset(or_2_out));  // open: Qn, preset, en
  or or_3 (or_3_out, Clear, and_3_out);
  T_Flip_Flop #(.trigger("falling")) t_ff_9 (
    .clk(and_4_out), .T(1'b1), .Q(D), .reset(or_3_out));  // open: Qn, preset, en
  T_Flip_Flop #(.trigger("falling")) t_ff_10 (.clk(D), .T(1'b1), .Q(C), .reset(or_3_out));  // open: Qn, preset, en
  not not_5 (not_5_out, B);
  not not_6 (not_6_out, D);
  and and_3 (and_3_out, not_6_out, C, not_5_out, A);
  T_Flip_Flop #(.trigger("falling")) t_ff_11 (.clk(C), .T(1'b1), .Q(B), .reset(or_3_out));  // open: Qn, preset, en
  T_Flip_Flop #(.trigger("falling")) t_ff_12 (.clk(B), .T(1'b1), .Q(A), .reset(or_3_out));  // open: Qn, preset, en
  or or_4 (or_4_out, Clear_3, and_4_out);
  T_Flip_Flop #(.trigger("falling")) t_ff_13 (.clk(Fin), .T(1'b1), .Q(D_3), .reset(or_4_out));  // open: Qn, preset, en
  T_Flip_Flop #(.trigger("falling")) t_ff_14 (.clk(D_3), .T(1'b1), .Q(C_3), .reset(or_4_out));  // open: Qn, preset, en
  not not_7 (not_7_out, D_3);
  not not_8 (not_8_out, B_3);
  and and_4 (and_4_out, not_7_out, C_3, not_8_out, A_3);
  T_Flip_Flop #(.trigger("falling")) t_ff_15 (.clk(C_3), .T(1'b1), .Q(B_3), .reset(or_4_out));  // open: Qn, preset, en
  T_Flip_Flop #(.trigger("falling")) t_ff_16 (.clk(B_3), .T(1'b1), .Q(A_3), .reset(or_4_out));  // open: Qn, preset, en

  // Notes on the sheet:
  //   sequencia de quatro contadores de 0 - 9  unidades dezenas centanas e milhares
endmodule

module mudaMes (
  input  in_1,
  input  in_2,
  input  in_3,
  input  in_4,
  input  in_5,
  input  in_6,
  input  in_7,
  input  in_8,
  input  in_9,
  input  in_10,
  input  in_11,
  input  in_12,
  output out_13
);

  wire and_1_out, and_2_out, and_3_out, and_4_out, and_5_out, and_6_out, and_7_out, and_8_out, and_9_out,
       and_10_out, not_1_out, not_2_out, not_3_out, not_4_out, not_5_out, not_6_out, not_7_out, not_8_out,
       not_9_out, not_10_out, not_11_out, not_12_out, not_13_out, not_14_out, not_15_out, not_16_out,
       not_17_out, not_18_out, not_19_out, not_20_out, not_21_out, not_22_out, not_23_out, not_24_out,
       not_25_out, not_26_out, not_27_out, not_28_out, not_29_out, not_30_out, not_31_out, not_32_out,
       or_1_out;

  not not_1 (not_1_out, in_5);
  not not_2 (not_2_out, in_4);
  and and_1 (and_1_out, in_6, not_1_out, not_2_out, not_3_out, in_2, in_1);
  not not_3 (not_3_out, in_3);
  not not_4 (not_4_out, in_6);
  not not_5 (not_5_out, in_5);
  not not_6 (not_6_out, in_4);
  and and_2 (and_2_out, not_4_out, not_5_out, not_6_out, not_7_out, in_2, in_1);
  not not_7 (not_7_out, in_3);
  not not_8 (not_8_out, in_12);
  not not_9 (not_9_out, in_11);
  not not_10 (not_10_out, in_9);
  not not_11 (not_11_out, in_8);
  not not_12 (not_12_out, in_7);
  not not_13 (not_13_out, in_12);
  not not_14 (not_14_out, in_9);
  not not_15 (not_15_out, in_8);
  not not_16 (not_16_out, in_7);
  not not_17 (not_17_out, in_11);
  not not_18 (not_18_out, in_10);
  not not_19 (not_19_out, in_8);
  not not_20 (not_20_out, in_7);
  not not_21 (not_21_out, in_11);
  not not_22 (not_22_out, in_10);
  not not_23 (not_23_out, in_9);
  not not_24 (not_24_out, in_7);
  not not_25 (not_25_out, in_5);
  not not_26 (not_26_out, in_4);
  and and_3 (and_3_out, in_6, not_25_out, not_26_out, in_3, not_27_out, in_1);
  not not_27 (not_27_out, in_2);
  not not_28 (not_28_out, in_12);
  not not_29 (not_29_out, in_10);
  and and_4 (and_4_out, not_28_out, in_11, not_29_out, not_30_out, not_31_out, not_32_out);
  not not_30 (not_30_out, in_9);
  not not_31 (not_31_out, in_8);
  not not_32 (not_32_out, in_7);
  and and_5 (and_5_out, not_8_out, not_9_out, in_10, not_10_out, not_11_out, not_12_out);
  and and_6 (and_6_out, not_13_out, in_11, in_10, not_14_out, not_15_out, not_16_out);
  and and_7 (and_7_out, in_12, not_17_out, not_18_out, in_9, not_19_out, not_20_out);
  and and_8 (and_8_out, in_12, not_21_out, not_22_out, not_23_out, in_8, not_24_out);
  and and_9 (and_9_out, and_3_out, and_4_out);
  or or_1 (or_1_out, and_5_out, and_6_out, and_7_out, and_8_out);
  or or_2 (out_13, and_9_out, and_1_out, and_10_out);
  and and_10 (and_10_out, or_1_out, and_2_out);

  // Notes on the sheet:
  //   verifica se dia == 31
  //   verifica se dia == 30
  //   verifica se dia ==28
  //   verifica se mes ==2
  //   confere se está no mes de 30 dias
  //   se dia == 29 no mes dois dispara o resetador
  //   se dia ==30 e o mes for de 30 reseta
endmodule
