// Logisim project Questão3.circ as structural Verilog: 3 circuits, main circuit main
module main (
  input  S0,
  input  S1,
  input  S2,
  input  S3,
  input  S4
);

  wire display7_1_a_2, display7_1_b_2, display7_1_c_2, display7_1_d_2, display7_1_e, display7_1_f,
       display7_1_g, n2_entre_5_1_a, n2_entre_5_1_b, n2_entre_5_1_c, n2_entre_5_1_d;

  _2_entre_5 u_2_entre_5_1 (
    .S0(S0), .S1(S1), .S2(S2), .S3(S3), .S4(S4), .A(n2_entre_5_1_a), .B(n2_entre_5_1_b), .C(n2_entre_5_1_c),
    .D(n2_entre_5_1_d));
  _7_Segment_Display u_7_segment_display_1 (
    .g(display7_1_g), .f(display7_1_f), .a(display7_1_a_2), .b(display7_1_b_2), .e(display7_1_e),
    .d(display7_1_d_2), .c(display7_1_c_2));  // open: dp
  Display7 display7_1 (
    .A(n2_entre_5_1_a), .B(n2_entre_5_1_b), .C(n2_entre_5_1_c), .D(n2_entre_5_1_d), .a_2(display7_1_a_2),
    .b_2(display7_1_b_2), .c_2(display7_1_c_2), .d_2(display7_1_d_2), .e(display7_1_e), .f(display7_1_f),
    .g(display7_1_g));
endmodule

module _2_entre_5 (
  input  S0,
  input  S1,
  input  S2,
  input  S3,
  input  S4,
  output A,
  output B,
  output C,
  output D
);

  wire and_1_out, and_2_out, and_3_out, and_4_out, and_5_out, and_6_out, and_8_out, and_9_out, and_10_out,
       and_11_out, and_12_out, and_13_out, nor_1_out, nor_2_out, nor_3_out, nor_4_out, nor_5_out, nor_6_out,
       nor_7_out, nor_8_out, nor_9_out, nor_10_out, nor_11_out, nor_12_out, nor_13_out, nor_14_out;

  nor nor_1 (nor_1_out, S0, S0);
  nor nor_2 (nor_2_out, S1, S1);
  nor nor_3 (nor_3_out, S2, S2);
  nor nor_4 (nor_4_out, S3, S3);
  nor nor_5 (nor_5_out, S0, S0);
  nor nor_6 (nor_6_out, S0, S0);
  nor nor_7 (nor_7_out, S1, S1);
  nor nor_8 (nor_8_out, S0, S0);
  nor nor_9 (nor_9_out, S2, S2);
  and and_1 (and_1_out, nor_1_out, nor_2_out);
  and and_2 (and_2_out, nor_3_out, nor_4_out);
  and and_3 (and_3_out, nor_5_out, S3);
  nor nor_10 (nor_10_out, S4, S4);
  and and_4 (and_4_out, nor_6_out, S1);
  nor nor_11 (nor_11_out, S3, S3);
  and and_5 (and_5_out, S0, nor_7_out);
  nor nor_12 (nor_12_out, S2, S2);
  nor nor_13 (nor_13_out, S1, S1);
  nor nor_14 (nor_14_out, S4, S4);
  and and_6 (and_6_out, nor_8_out, nor_9_out);
  and and_7 (A, and_1_out, S4);
  and and_8 (and_8_out, and_2_out, S4);
  or or_1 (B, and_8_out, and_9_out);
  and and_9 (and_9_out, and_3_out, nor_10_out);
  and and_10 (and_10_out, and_4_out, nor_11_out);
  or or_2 (C, and_10_out, and_11_out);
  and and_11 (and_11_out, and_5_out, nor_12_out);
  and and_12 (and_12_out, nor_13_out, nor_14_out);
  or or_3 (D, and_12_out, and_13_out);
  and and_13 (and_13_out, and_6_out, S4);
endmodule

module Display7 (
  input  A,
  input  B,
  input  C,
  input  D,
  output a_2,
  output b_2,
  output c_2,
  output d_2,
  output e,
  output f,
  output g
);

  wire and_1_out, and_2_out, and_3_out, and_4_out, and_5_out, and_6_out, and_7_out, and_8_out, and_9_out,
       and_10_out, and_11_out, and_12_out, and_13_out, nor_1_out, nor_2_out, nor_3_out, nor_4_out, not_1_out,
       not_2_out, not_3_out, not_4_out, not_5_out, not_6_out, not_7_out, not_8_out, not_9_out, not_10_out,
       not_11_out, not_12_out, not_13_out, or_1_out, or_3_out, or_6_out, or_8_out, xnor_1_out, xor_1_out;

  or or_1 (or_1_out, A, C);
  or or_2 (a_2, or_1_out, xnor_1_out);
  xnor xnor_1 (xnor_1_out, B, D);
  nor nor_1 (nor_1_out, D, D);
  nor nor_2 (nor_2_out, B, B);
  or or_3 (or_3_out, nor_2_out, and_2_out);
  nor nor_3 (nor_3_out, C, C);
  and and_1 (and_1_out, D, C);
  and and_2 (and_2_out, nor_1_out, nor_3_out);
  or or_4 (b_2, or_3_out, and_1_out);
  nor nor_4 (nor_4_out, C, C);
  or or_5 (c_2, nor_4_out, B, D);
  not not_1 (not_1_out, D);
  not not_2 (not_2_out, B);
  not not_3 (not_3_out, B);
  and and_3 (and_3_out, not_2_out, not_1_out);
  or or_6 (or_6_out, A, and_3_out);
  or or_7 (d_2, or_6_out, and_5_out, or_8_out);
  not not_4 (not_4_out, D);
  and and_4 (and_4_out, C, not_4_out);
  and and_5 (and_5_out, not_3_out, C);
  or or_8 (or_8_out, and_4_out, and_6_out);
  not not_5 (not_5_out, C);
  and and_6 (and_6_out, B, not_5_out, D);
  not not_6 (not_6_out, D);
  not not_7 (not_7_out, B);
  and and_7 (and_7_out, not_7_out, not_6_out);
  not not_8 (not_8_out, D);
  and and_8 (and_8_out, C, not_8_out);
  and and_9 (and_9_out, B, A);
  or or_9 (e, and_7_out, and_8_out, and_9_out);
  not not_9 (not_9_out, D);
  not not_10 (not_10_out, C);
  and and_10 (and_10_out, not_10_out, not_9_out);
  not not_11 (not_11_out, C);
  and and_11 (and_11_out, not_11_out, B);
  or or_10 (f, A, and_10_out, and_11_out, and_12_out);
  not not_12 (not_12_out, D);
  not not_13 (not_13_out, D);
  and and_12 (and_12_out, B, not_13_out);
  and and_13 (and_13_out, not_12_out, C);
  or or_11 (g, A, and_13_out, xor_1_out);
  xor xor_1 (xor_1_out, C, B);
endmodule
